# Fritzing sketch Placarduino (saved by Fritzing 0.9.2b)
breadboards: 1

parts:
  Componente1 = Arduino Uno (Rev3) - ICSP
  S1 = Pushbutton [package="[THT]"]
  S2 = Pushbutton [package="[THT]"]
  R3 = Resistor [tolerance=±5% resistance=10k package=THT]
  R4 = Resistor [tolerance=±5% resistance=10k package=THT]
  Piezo2 = Piezo Speaker
  R5 = Resistor [tolerance=±5% resistance=220 package=THT]
  LCM1602_IIC1 = LCM1602 IIC [part_number="LCM1602 IIC" chip_label="LCM1602 IIC" package="DIP (Dual Inline) [THT]"]
  LCD1 = LCD screen
  S3 = Pushbutton [package="[THT]"]
  S4 = Pushbutton [package="[THT]"]
  R6 = Resistor [tolerance=±5% resistance=10k package=THT]
  R7 = Resistor [tolerance=±5% resistance=10k package=THT]
  Componente2 = RFID-RC522-v3
  LED1 = LED - 5mm [color="Green (555nm)" package="5 mm [THT]"]
  R8 = Resistor [tolerance=±5% resistance=300 package=THT]
  S5 = Pushbutton [package="[THT]"]
  R9 = Resistor [tolerance=±5% resistance=10k package=THT]

nets:
  N1: Componente1.A4/SDA, LCM1602_IIC1.SDA
  N2: Componente1.A5/SCL, LCM1602_IIC1.SCL
  N3: Componente1.D8, S5.Pin_1, S5.Pin_2, R9.Pin_1
  N4: Componente1.D9_PWM, Componente2.RST
  N5: Componente1.D10_PWM/SS, Componente2.SDA
  N6: Componente1.D11_PWM/MOSI, Componente2.MOSI
  N7: Componente1.D12/MISO, Componente2.MISO
  N8: Componente1.D13/SCK, Componente2.SCK
  N9: Componente1.D3_PWM, R5.Pin_0, R8.Pin_0
  N10: Componente1.D4, S4.Pin_1, S4.Pin_2, R6.Pin_1
  N11: Componente1.D5_PWM, S2.Pin_1, S2.Pin_2, R4.Pin_1
  N12: Componente1.D6_PWM, R3.Pin_1, S3.Pin_1, S3.Pin_2
  N13: Componente1.D7, S1.Pin_1, S1.Pin_2, R7.Pin_1
  3V3: Componente1.3V3, Componente2.3.3V
  5V: Componente1.5V, S1.Pin_3, S1.Pin_4, S2.Pin_3, S2.Pin_4, LCM1602_IIC1.VCC, S3.Pin_3, S3.Pin_4, S4.Pin_3, S4.Pin_4, S5.Pin_3, S5.Pin_4
  GND: Componente1.GND, R3.Pin_0, R4.Pin_0, Piezo2.GND, LCM1602_IIC1.GND, R6.Pin_0, R7.Pin_0, Componente2.GND, LED1.cathode, R9.Pin_0
  N14: Piezo2.VCC, R5.Pin_1
  VSS: LCM1602_IIC1.VSS, LCD1.VSS
  VDD: LCM1602_IIC1.VDD, LCD1.VDD
  N15: LCM1602_IIC1.V0, LCD1.V0
  N16: LCM1602_IIC1.RS, LCD1.RS
  N17: LCM1602_IIC1.RW, LCD1.R/W
  N18: LCM1602_IIC1.E, LCD1.E
  N19: LCM1602_IIC1.D0, LCD1.DB0
  N20: LCM1602_IIC1.D1, LCD1.DB1
  N21: LCM1602_IIC1.D2, LCD1.DB2
  N22: LCM1602_IIC1.D3, LCD1.DB3
  N23: LCM1602_IIC1.D4, LCD1.DB4
  N24: LCM1602_IIC1.D5, LCD1.DB5
  N25: LCM1602_IIC1.D6, LCD1.DB6
  N26: LCM1602_IIC1.D7, LCD1.DB7
  N27: LCM1602_IIC1.A, LCD1.LED+
  N28: LCM1602_IIC1.K, LCD1.LED-
  N29: LCM1602_IIC1.LED_A, LCM1602_IIC1.LED_B
  N30: LED1.anode, R8.Pin_1

notes:
  Geralmente o controlador é soldado atrás do display, mas não existe um componente assim no Fritzing.
  O Fritzing também não tem um display 20x4, mas os pinos são os mesmos do 16x2
  Da esquerda para direita:
  Reduzir pontos do jogador 1 (pino 7)
  Aumentar pontos do jogador 1 (pino 6)
  Reduzir pontos do jogador 2 (pino 5)
  Aumentar pontos do jogador 2 (pino 4)

custom parts:
  Piezo Speaker: This is a small 12mm round speaker that operates around the audible 2kHz range. You can use these speakers to create simple music or user interfaces.
  LCM1602 IIC: I2C-Module to use a 1602 or 2004 LCD on with the wire.h libory Serial LCD Modul
  RFID-RC522-v3: A simple China made RFID-RC522 Reader (6x4 cm); do check the pin labels, as this is a MFRC522 based clone.
