# Fritzing sketch Standalone (saved by Fritzing 0.9.3b)
circuit board: 7cm x 5cm
circuit board: 1.34333cm x 3.67cm
breadboards: 1
perfboards: 4

parts:
  Atmega = atmega328 [package=dip]
  R_RST = Resistor [tolerance=±5% resistance=10k package=THT]
  XTAL16M = Crystal [frequency="16 Mhz" package=THT]
  C2 = Ceramic Capacitor [capacitance=22pF voltage=16V package="100 mil [THT, multilayer]"]
  BT_RST = Pushbutton [package="[THT]"]
  BT_DEC1 = Pushbutton [package="[THT]"]
  BT_INC1 = Pushbutton [package="[THT]"]
  BT_DEC2 = Pushbutton [package="[THT]"]
  BT_INC2 = Pushbutton [package="[THT]"]
  C1 = Ceramic Capacitor [capacitance=22pF voltage=16V package="100 mil [THT, multilayer]"]
  R_INC1 = Resistor [tolerance=±5% resistance=10k package=THT]
  R_DEC1 = Resistor [tolerance=±5% resistance=10k package=THT]
  R_DEC2 = Resistor [tolerance=±5% resistance=10k package=THT]
  BUZ = Piezo Speaker
  LED = LED - 5mm [color="Green (555nm)" package="5 mm [THT]"]
  R_BUZ = Resistor [tolerance=±5% resistance=220 package=THT]
  R_LED = Resistor [tolerance=±5% resistance=300 package=THT]
  BT_WIN = Pushbutton [package="[THT]"]
  R_WIN = Resistor [tolerance=±5% resistance=10k package=THT]
  RFID = RFID-RC522-v3
  R_INC2 = Resistor [tolerance=±5% resistance=10k package=THT]
  LCM1602_IIC = LCM1602 IIC [part_number="LCM1602 IIC" chip_label="LCM1602 IIC" package="DIP (Dual Inline) [THT]"]
  LCD = LCD screen
  GND = Pad [width=3.2 height=3.2 connect=center]
  IN = Pad [width=2.54 height=2.54 connect=center]  # not connected
  BT_WIN1 = Pushbutton [package="[THT]"]
  BUZ2 = Piezo Speaker
  LED2 = LED - 5mm [color="Green (555nm)" package="5 mm [THT]"]
  R_WIN1 = Resistor [tolerance=±5% resistance=10k package=THT]
  J2 = male pin header, 4 pins [form="♂ (male)"]
  R_LED1 = Resistor [tolerance=±5% resistance=300 package=THT]
  R_BUZ1 = Resistor [tolerance=±5% resistance=220 package=THT]
  BT_DEC3 = Pushbutton [package="[THT]"]
  BT_DEC4 = Pushbutton [package="[THT]"]
  J3 = male pin header, 4 pins [form="♂ (male)"]
  R_INC3 = Resistor [tolerance=±5% resistance=10k package=THT]
  R_INC4 = Resistor [tolerance=±5% resistance=10k package=THT]
  R_INC5 = Resistor [tolerance=±5% resistance=10k package=THT]
  R_INC6 = Resistor [tolerance=±5% resistance=10k package=THT]
  BT_DEC5 = Pushbutton [package="[THT]"]
  BT_DEC6 = Pushbutton [package="[THT]"]
  J5 = male pin header, 4 pins [form="♂ (male)"]
  J20 = male pin header, 4 pins [form="♂ (male)"]
  J21 = male pin header, 4 pins [form="♂ (male)"]
  J22 = male pin header, 4 pins [form="♂ (male)"]
  J23 = male pin header, 4 pins [form="♂ (male)"]
  R_RST2 = Resistor [tolerance=±5% resistance=10k package=THT]
  XTAL16M3 = Crystal [frequency="16 Mhz" package=THT]
  J24 = male pin header, 2 pins [form="♂ (male)"]
  J25 = male pin header, 7 pins [form="♂ (male)"]
  R_RST3 = Resistor [tolerance=±5% resistance=220 package=THT]
  LED3 = LED - 3mm [color="Red (633nm)" package="3 mm [THT]"]
  S1 = Pushbutton [package="[THT]"]
  IC3 = Voltage Regulator [package=to220-igo]
  C14 = Ceramic Capacitor top view [package="100 mil [THT, multilayer]"]
  C15 = Electrolytic Capacitor top view [package="100 mil [THT, electrolytic]"]
  U1 = 7805 [package=to220-igo]
  C16 = Ceramic Capacitor top view [package="100 mil [THT, multilayer]"]
  Atmega3 = atmega328 [package=dip]

nets:
  N1: Atmega.RESET, R_RST.Pin_0, BT_RST.Pin_1, BT_RST.Pin_2
  Feedback: Atmega.D3_(PWM), R_BUZ.Pin_0, R_LED.Pin_1
  BtWin: Atmega.D4, BT_WIN.Pin_1, BT_WIN.Pin_2, R_WIN.Pin_1
  5V: Atmega.VCC, Atmega.AVCC, Atmega.AREF, R_RST.Pin_1, BT_DEC1.Pin_3, BT_DEC1.Pin_4, BT_INC1.Pin_3, BT_INC1.Pin_4, BT_DEC2.Pin_3, BT_DEC2.Pin_4, BT_INC2.Pin_3, BT_INC2.Pin_4, BT_WIN.Pin_3, BT_WIN.Pin_4, LCM1602_IIC.VCC, IC3.IN
  GND: Atmega.GND, C2.1, BT_RST.Pin_3, BT_RST.Pin_4, C1.0, R_INC1.Pin_0, R_DEC1.Pin_0, R_DEC2.Pin_0, BUZ.GND, LED.cathode, R_WIN.Pin_0, RFID.GND, R_INC2.Pin_0, LCM1602_IIC.GND, GND.pad, IC3.GND
  N2: Atmega.XLAT1, XTAL16M.pin_0, C1.1
  N3: Atmega.XLAT2, XTAL16M.pin_1, C2.0
  BtDec1: Atmega.D5_(PWM), BT_DEC1.Pin_1, BT_DEC1.Pin_2, R_DEC1.Pin_1
  BtInc1: Atmega.D6_(PWM), BT_INC1.Pin_1, BT_INC1.Pin_2, R_INC1.Pin_1
  BtDec2: Atmega.D7, BT_DEC2.Pin_1, BT_DEC2.Pin_2, R_DEC2.Pin_1
  BtInc2: Atmega.D8, BT_INC2.Pin_1, BT_INC2.Pin_2, R_INC2.Pin_1
  RF_RST: Atmega.D9_(PWM), RFID.RST
  RF_SDA: Atmega.D10_(PWM), RFID.SDA
  RF_MOSI: Atmega.D11_(PWM), RFID.MOSI
  RF_MISO: Atmega.D12, RFID.MISO
  RF_SCK: Atmega.D13, RFID.SCK
  LCD_SDA: Atmega.A4, LCM1602_IIC.SDA
  LCD_SCL: Atmega.A5, LCM1602_IIC.SCL
  N4: BUZ.VCC, R_BUZ.Pin_1
  N5: LED.anode, R_LED.Pin_0
  N6: RFID.3.3V, IC3.OUT
  VSS: LCM1602_IIC.VSS, LCD.VSS
  VDD: LCM1602_IIC.VDD, LCD.VDD
  N7: LCM1602_IIC.V0, LCD.V0
  N8: LCM1602_IIC.RS, LCD.RS
  N9: LCM1602_IIC.RW, LCD.R/W
  N10: LCM1602_IIC.E, LCD.E
  N11: LCM1602_IIC.D0, LCD.DB0
  N12: LCM1602_IIC.D1, LCD.DB1
  N13: LCM1602_IIC.D2, LCD.DB2
  N14: LCM1602_IIC.D3, LCD.DB3
  N15: LCM1602_IIC.D4, LCD.DB4
  N16: LCM1602_IIC.D5, LCD.DB5
  N17: LCM1602_IIC.D6, LCD.DB6
  N18: LCM1602_IIC.D7, LCD.DB7
  N19: LCM1602_IIC.A, LCD.LED+
  N20: LCM1602_IIC.K, LCD.LED-
  N21: LCM1602_IIC.LED_A, LCM1602_IIC.LED_B
  N22: BT_WIN1.Pin_1, BT_WIN1.Pin_2, J2.pin1
  N23: BT_WIN1.Pin_3, BT_WIN1.Pin_4, R_WIN1.Pin_1, J2.pin4
  N24: BUZ2.GND, LED2.cathode, R_WIN1.Pin_0, J2.pin2
  N25: BUZ2.VCC, R_BUZ1.Pin_0
  N26: LED2.anode, R_LED1.Pin_0
  N27: J2.pin3, R_LED1.Pin_1, R_BUZ1.Pin_1
  N28: BT_DEC3.Pin_1, BT_DEC3.Pin_2, J3.pin4, R_INC4.Pin_0
  N29: BT_DEC3.Pin_3, BT_DEC3.Pin_4, BT_DEC4.Pin_3, BT_DEC4.Pin_4, J3.pin1
  N30: BT_DEC4.Pin_1, BT_DEC4.Pin_2, J3.pin3, R_INC3.Pin_1
  N31: J3.pin2, R_INC3.Pin_0, R_INC4.Pin_1
  N32: R_INC5.Pin_0, BT_DEC6.Pin_3, BT_DEC6.Pin_4, J5.pin1
  N33: R_INC5.Pin_1, R_INC6.Pin_0, J5.pin3
  N34: R_INC6.Pin_1, BT_DEC5.Pin_3, BT_DEC5.Pin_4, J5.pin2
  N35: BT_DEC5.Pin_1, BT_DEC5.Pin_2, BT_DEC6.Pin_1, BT_DEC6.Pin_2, J5.pin4
  N36: J20.pin1, Atmega3.A5
  N37: J20.pin2, Atmega3.A4
  GND_2: J20.pin3, J21.pin2, J22.pin2, J23.pin2, J24.pin2, J25.pin7, LED3.cathode, S1.Pin_1, S1.Pin_2, C14.1, C15.-, U1.GND, C16.1, Atmega3.GND
  N38: J20.pin4, J21.pin1, J22.pin1, J23.pin1, R_RST2.Pin_1, J24.pin1, R_RST3.Pin_1, U1.IN, Atmega3.VCC, Atmega3.AVCC, Atmega3.AREF
  N39: J21.pin3, Atmega3.D3_(PWM)
  N40: J21.pin4, Atmega3.D4
  N41: J22.pin3, Atmega3.D5_(PWM)
  N42: J22.pin4, Atmega3.D6_(PWM)
  N43: J23.pin3, Atmega3.D8
  N44: J23.pin4, Atmega3.D7
  N45: R_RST2.Pin_0, S1.Pin_3, S1.Pin_4, Atmega3.RESET
  N46: XTAL16M3.pin_0, C16.0, Atmega3.XLAT1
  N47: XTAL16M3.pin_1, C14.0, Atmega3.XLAT2
  N48: J25.pin1, Atmega3.D9_(PWM)
  N49: J25.pin2, Atmega3.D10_(PWM)
  N50: J25.pin3, Atmega3.D11_(PWM)
  N51: J25.pin4, Atmega3.D12
  N52: J25.pin5, Atmega3.D13
  N53: J25.pin6, C15.+, U1.OUT
  N54: R_RST3.Pin_0, LED3.anode

notes:
  5V GND BUZ WIN
  Feedback & gameover
  5V GND INC DEC
  Controles de jogador
  DEC INC GND 5V

custom parts:
  Piezo Speaker: This is a small 12mm round speaker that operates around the audible 2kHz range. You can use these speakers to create simple music or user interfaces.
  RFID-RC522-v3: A simple China made RFID-RC522 Reader (6x4 cm); do check the pin labels, as this is a MFRC522 based clone.
  LCM1602 IIC: I2C-Module to use a 1602 or 2004 LCD on with the wire.h libory Serial LCD Modul
  Voltage Regulator: Voltage Regulator Standard 7805 5V regulator. IGO (Input Ground Output). Spark Fun Electronics SKU : COM-00107
  Ceramic Capacitor top view: 100 nF multilayer Ceramic Capacitor breadboard set to top view for perfboard use.
  Electrolytic Capacitor top view: A small electrolytic capacitor breadboard top view for use on perf board
  7805: Voltage Regulator Standard 7805 5V regulator. IGO (Input Ground Output). Breadboard view modified for top view (i.e. so it will fit on perfboard without obstructing other components which makes it look a little odd ...).
